# Fritzing sketch EMOONv1BreadBoardSketch (saved by Fritzing 0.9.3b)
breadboards: 1

parts:
  U1 = NodeMCU V1.0
  Part1 = Arduino Mega ADK (Rev3)
  PIR1 = PIR sensor
  M1 = Stepper Motor - Unipolar
  LED2 = RGB LED - (4 legs) [package="5 mm [THT]"]
  M2 = DC Motor
  R2 = Resistor [tolerance=±5% resistance=330 package=THT]
  DHT1 = DHT22 Humidity and Temperature Sensor
  SERVO1 = Tower Pro SG90 servo [part_number=101246]
  LED3 = LEDs [package=led10mm]
  LED4 = LED - 5mm [color="Red (633nm)" package="5 mm [THT]"]
  Q2 = npn-Powertransistor [package="TO220 [THT]"]
  VCC1 = Battery
  ULN2003A_-_Stepper_Driver_Board1 = ULN2003A - Stepper Driver Board [package=board]
  e-radionica_com1 = LM393 LDR breakout [part_number=100027]
  R3 = Resistor [tolerance=±5% resistance=3.3k package=THT]
  R4 = Resistor [tolerance=±5% resistance=3.3k package=THT]
  R5 = Resistor [tolerance=±5% resistance=330 package=THT]
  Q3 = npn-Powertransistor [package="TO220 [THT]"]
  R6 = Resistor [tolerance=±5% resistance=3.3k package=THT]
  R7 = Resistor [tolerance=±5% resistance=330 package=THT]
  Q4 = npn-Powertransistor [package="TO220 [THT]"]
  R8 = Resistor [tolerance=±5% resistance=3.3k package=THT]
  R9 = Resistor [tolerance=±5% resistance=330 package=THT]
  Q5 = npn-Powertransistor [package="TO220 [THT]"]
  R10 = Resistor [tolerance=±5% resistance=3.3k package=THT]
  R11 = Resistor [tolerance=±5% resistance=330 package=THT]
  Q6 = npn-Powertransistor [package="TO220 [THT]"]
  R12 = Resistor [tolerance=±5% resistance=330 package=THT]

nets:
  N1: U1.D1, e-radionica_com1.DO
  N2: U1.D3, DHT1.DATA
  N3: U1.D4, PIR1.SIG
  VDD: U1.3V3, Part1.5V, PIR1.VDD, DHT1.VDD, SERVO1.+5V, e-radionica_com1.VCC
  GND: U1.GND, Part1.GND, PIR1.GND, DHT1.GND, SERVO1.GND, Q2.emitter, VCC1.-, e-radionica_com1.GND, Q3.emitter, Q4.emitter, Q5.emitter, Q6.emitter, R12.Pin_0
  N4: U1.D7, Part1.D15/RX3
  N5: U1.D8, Part1.D14/TX3
  N6: Part1.D24, R10.Pin_1
  N7: Part1.D25, R8.Pin_1
  N8: Part1.D26, R6.Pin_1
  N9: Part1.D27, R4.Pin_1
  N10: Part1.D28, LED3.A
  N11: Part1.D34, ULN2003A_-_Stepper_Driver_Board1.IN1
  N12: Part1.D35, ULN2003A_-_Stepper_Driver_Board1.IN2
  N13: Part1.D36, ULN2003A_-_Stepper_Driver_Board1.IN3
  N14: Part1.D37, ULN2003A_-_Stepper_Driver_Board1.IN4
  N15: Part1.D42, R3.Pin_1
  N16: Part1.D43, SERVO1.Signal
  N17: M1.A, ULN2003A_-_Stepper_Driver_Board1.B
  N18: M1.COMMON_1, ULN2003A_-_Stepper_Driver_Board1.A
  N19: M1.C, ULN2003A_-_Stepper_Driver_Board1.E
  N20: M1.B, ULN2003A_-_Stepper_Driver_Board1.C
  N21: M1.COMMON_2, ULN2003A_-_Stepper_Driver_Board1.D
  N22: M1.D, ULN2003A_-_Stepper_Driver_Board1.F
  N23: LED2.red_cathode, R11.Pin_0
  N24: LED2.common_anode, M2.pin_2, LED4.anode, VCC1.+
  N25: LED2.green_cathode, R9.Pin_0
  N26: LED2.blue_cathode, R7.Pin_0
  N27: M2.pin_1, R2.Pin_0
  N28: R2.Pin_1, Q2.collector
  N29: LED3.C, R12.Pin_1
  N30: LED4.cathode, R5.Pin_0
  N31: Q2.base, R3.Pin_0
  N32: R4.Pin_0, Q3.base
  N33: R5.Pin_1, Q3.collector
  N34: R6.Pin_0, Q4.base
  N35: R7.Pin_1, Q4.collector
  N36: R8.Pin_0, Q5.base
  N37: R9.Pin_1, Q5.collector
  N38: R10.Pin_0, Q6.base
  N39: R11.Pin_1, Q6.collector

notes:
  5V Power Rail
  3.3V
  Power
  9-12V Power Rail
  Fan Motor
  Main Lights
  RGB Lights
  Warm Lights

custom parts:
  NodeMCU V1.0: ESP8266 based NodeMCU
  Tower Pro SG90 servo: Original file by John De Cristofaro http://www.adafruit.com/products/1449 Adafruit Feedback Servo (Small) Edited by: e-radionica.com 28/9/2015
  ULN2003A - Stepper Driver Board: A common stepper motor driver board based on ULN2003APG darlington array
